# Fritzing sketch Untitled Sketch 2 (saved by Fritzing 0.9.3b)
breadboards: 1

parts:
  U1 = attiny85 [package=dip]
  LED1 = RGB LED (com. anode, rbg) [package="5 mm [THT]"]

nets:
  N1: U1.Pin_2, LED1.red_cathode
  N2: U1.Pin_3, LED1.blue_cathode
  N3: U1.Pin_7, LED1.green_cathode
  N4: U1.Pin_8, LED1.common_anode
